# Fritzing sketch scrummasterlcd-schematic (saved by Fritzing 0.9.2b)
breadboards: 1

parts:
  LCD1 = LCD screen
  Onderdeel1 = Arduino Uno (Rev3)
  S1 = Pushbutton [package="[THT]"]
  LED1 = LED - 5mm [color="Red (660nm)" package="5 mm [THT]"]
  LED2 = LED - 5mm [color="Green (570nm)" package="5 mm [THT]"]
  LED3 = LED - 5mm [color="Yellow (592nm)" package="5 mm [THT]"]
  J1 = Piezo Speaker
  R2 = Resistor [tolerance=±5% resistance=10k package=THT]
  R3 = Resistor [tolerance=±5% resistance=220 package=THT]
  R4 = Resistor [tolerance=±5% resistance=220 package=THT]
  R5 = Resistor [tolerance=±5% resistance=220 package=THT]
  R6 = Resistor [tolerance=±5% resistance=220 package=THT]
  R1 = Resistor [tolerance=±5% resistance=1k package=THT]

nets:
  VSS: LCD1.VSS, LCD1.R/W, LCD1.LED-, Onderdeel1.GND, LED1.anode, LED3.anode, J1.pin1, R2.Pin_1, R1.Pin_1
  VDD: LCD1.VDD, Onderdeel1.5V, S1.Pin_3, S1.Pin_4, R6.Pin_1
  N1: LCD1.V0, R1.Pin_0
  N2: LCD1.RS, Onderdeel1.D7
  N3: LCD1.E, Onderdeel1.D8
  N4: LCD1.DB4, Onderdeel1.D9_PWM
  N5: LCD1.DB5, Onderdeel1.D10_PWM/SS
  N6: LCD1.DB6, Onderdeel1.D11_PWM/MOSI
  N7: LCD1.DB7, Onderdeel1.D12/MISO
  N8: LCD1.LED+, R6.Pin_0
  N9: Onderdeel1.D13/SCK, J1.pin2
  N10: Onderdeel1.D2, S1.Pin_1, S1.Pin_2, R2.Pin_0
  N11: Onderdeel1.D4, R3.Pin_1
  N12: Onderdeel1.D5_PWM, R4.Pin_1
  N13: Onderdeel1.D6_PWM, R5.Pin_1
  N14: LED1.cathode, LED2.anode, R3.Pin_0
  N15: LED2.cathode, R5.Pin_0
  N16: LED3.cathode, R4.Pin_0

// code stored in the sketch: scrummasterlcd.ino
#include <LiquidCrystal.h>

//TEAM
String team[] = {"Nicolas", "Rabha", "Baptiste", "Davy", "Géraldine", "Stijn"};
const int TEAM_SIZE = 6;

const unsigned long SEC = 1000;
const unsigned long GREEN_DURATION=65*SEC;
const unsigned long YELLOW_DURATION=10*SEC;


const unsigned int RANDOM_ITER = 2500;

//non-LCD pins
const int BUTTON = 2;
const int SOUND_PIN = 13;
const int SOUND_LENGTH = 100;
const int TONE1 = 3000;
const int TONE2 = 2500;
const int NB_ALARM_SOUNDS=8;


//LCD pins
const int LCD_RS = 7;
const int LCD_ENABLE = 8;
const int LCD_D4 = 9;
const int LCD_D5 = 10;
const int LCD_D6 = 11;
const int LCD_D7 = 12;
LiquidCrystal lcd(LCD_RS, LCD_ENABLE, LCD_D4, LCD_D5, LCD_D6, LCD_D7);

//LED pins
const int GREEN_LED = 6;
const int YELLOW_LED = 5;
const int RED_LED = 4;

//custom characters
const byte EACUTE = 1;
const byte CCEDILLE = 2;

byte EACUTE_CHAR[8] = {
  B00010,
  B00100,
  B01110,
  B10001,
  B11111,
  B10000,
  B01110,
  B00000
};
byte CEDI_CHAR[8] = {
  B00000,
  B00000,
  B01110,
  B10000,
  B10000,
  B01110,
  B00100,
  B01100
};


// states
const int S_INITIAL = 0;
const int S_READY = 1;
const int S_GREEN = 2;
const int S_YELLOW = 3;
const int S_RED = 4;
const int S_FINISHED = 5;

//time management
unsigned long yellowTime = 0;
unsigned long redTime = 0;
unsigned long countdown_sec=0;


int nextTeamMemberIndex = 0;

boolean previousButtonState = false;
boolean buttonEventGenerated = false;
int currentState = S_INITIAL;

void setup() {
  pinMode(LCD_RS, OUTPUT);
  pinMode(LCD_ENABLE, OUTPUT);
  pinMode(LCD_D4, OUTPUT);
  pinMode(LCD_D5, OUTPUT);
  pinMode(LCD_D6, OUTPUT);
  pinMode(LCD_D7, OUTPUT);
  
  
  lcd.createChar(EACUTE, EACUTE_CHAR);
  lcd.createChar(CCEDILLE, CEDI_CHAR);
  lcd.begin(16, 2);
  
  //BUTTON setup
  pinMode(BUTTON, INPUT);
  
  pinMode(SOUND_PIN, OUTPUT);
  pinMode(RED_LED, OUTPUT);
  pinMode(YELLOW_LED, OUTPUT);
  pinMode(GREEN_LED, OUTPUT);
  
  
  
  allLedsOn();
  delay(400);
  allLedsOff();

  lcd.print("Press button to");
  lcd.setCursor(0, 1);
  lcd.print("shuffle");
  playInitialized();
}

void loop() {
  generateButtonEvent();
  if (buttonEvent()) {
    switch(currentState) {
      case S_INITIAL:
        shuffle();
        setReady();
        break;
      default:
        nextTeamMember();      
        break; 
    }
  }
  
  unsigned long now = millis();

  if ((currentState == S_GREEN) && (now >= yellowTime)) {
    showRemainingSeconds(now);
    setYellow();
  }
  if ((currentState == S_YELLOW) && (now >= redTime)) {
    showRemainingSeconds(now);
    setAlarm();
  }
  
  if ((currentState == S_GREEN) || (currentState == S_YELLOW) || (currentState==S_RED)) {
    showRemainingSeconds(now);
  }
}

void setGreen() {
  currentState = S_GREEN;
  ledOn(GREEN_LED);
}

void setYellow() {
  currentState = S_YELLOW;
  lcd.setCursor(4,1);
  lcd.write("end now");
  ledOn(YELLOW_LED);
  playWarning();
}

void setAlarm() {
  currentState = S_RED;
  lcd.setCursor(4,1);
  lcd.write("NEXT !!!");
  ledOn(RED_LED);
  playAlarm();
  
}

void showRemainingSeconds(unsigned long time) {
  
  unsigned long currentRemaining = getRemainingSeconds(time);
  if (currentRemaining != countdown_sec) {
    countdown_sec = currentRemaining;
    
    lcd.setCursor(14,0);
    if (countdown_sec < 10) {
      lcd.print(" ");
    }
    lcd.print(countdown_sec);
  }

}

unsigned long getRemainingSeconds(unsigned long time) {
  if (time >= redTime) {
    return 0;
  }
  return (redTime - time) / 1000 + 1;
  
}

void startCountDown() {
  unsigned long now = millis();
  yellowTime = now + GREEN_DURATION;
  redTime = yellowTime + YELLOW_DURATION;
  setGreen();  
}

void nextTeamMember() {
  if (nextTeamMemberIndex == TEAM_SIZE) {
    nextTeamMemberIndex = 0;
    setFinished();
  } else {
    showMember(team[nextTeamMemberIndex++]);
    startCountDown();
  }
}

void showMember(String member) {
    lcd.clear();
     
    int i = 0;
    while (i<member.length()) {
      String stringChar = String(member.charAt(i));
      //in case of UTF-8 is the first byte negative. Assume max utf8 length 2 bytes for char
      if (member.charAt(i) < 0) {
        stringChar.concat(member.charAt(i+1));
        i++;
      } 
      i++;
      printStringChar(stringChar);
    }
    lcd.setCursor(0,1);
}

void printStringChar(String charToPrint) {
  if (charToPrint.equals(String("é"))) {
    lcd.write(EACUTE);
  } else if (charToPrint.equals(String("ç"))) {
    lcd.write(CCEDILLE);
  } else {
    lcd.print(charToPrint);
  }
}

void shuffle() {
  lcd.clear();
  lcd.print("Shuffling...");
  randomSeed(millis());
  randomize(team);
}

void setReady() {
   lcd.clear();
   lcd.print("Ready to start");
   lcd.setCursor(0,1);
   lcd.print(TEAM_SIZE);
   lcd.print(" team members");
   currentState = S_READY;
   playReadyBeep();
}

void setFinished() {
  allLedsOff();
  lcd.clear();
  lcd.print("End of stand-up");
  lcd.setCursor(0,1);
  lcd.print("meeting");
  currentState = S_FINISHED;
  playReadyBeep();
}

void randomize(String array[]) {
  int a = 0;
  int b = 0;
  for (unsigned int i = 0; i < RANDOM_ITER; i++) {
    a = random(0, TEAM_SIZE);
    b = random(0, TEAM_SIZE);
    swap(array, a, b);
  }
}

void swap(String array[], int i, int j) {
  String swap = array[i];
  array[i] = array[j];
  array[j] = swap;
}

void generateButtonEvent() {
  boolean buttonPress = (digitalRead(BUTTON) == HIGH);
  if ((! buttonPress) && previousButtonState) {
    buttonEventGenerated = true;
  }
  previousButtonState = buttonPress;
}

boolean buttonEvent() {
  if (buttonEventGenerated) {
    buttonEventGenerated = false;
    return true;
  } else {
    return false;
  }
}

void playInitialized() {
    tone(SOUND_PIN, 600, 100);
    delay(100);
    tone(SOUND_PIN, 1000, 100);
}

void playWarning() {
   tone(SOUND_PIN, 5000, 25);
   delay(50);
   tone(SOUND_PIN, 5000, 25);
   delay(50);
}

void playAlarm() {
  for (int i = 0; i < NB_ALARM_SOUNDS; i++) {
    tone(SOUND_PIN, TONE1, SOUND_LENGTH);
    delay(SOUND_LENGTH);
    tone(SOUND_PIN, TONE2, SOUND_LENGTH);
    delay(SOUND_LENGTH);
  }
}

void playReadyBeep() {
  tone(SOUND_PIN, 2000, 200);
}

void allLedsOn() {
  digitalWrite(RED_LED, HIGH);
  digitalWrite(YELLOW_LED, HIGH);
  digitalWrite(GREEN_LED, HIGH);
}

void allLedsOff() {
  digitalWrite(RED_LED, LOW);
  digitalWrite(YELLOW_LED, LOW);
  digitalWrite(GREEN_LED, LOW);
}

void ledOn(int ledPin) {
  digitalWrite(RED_LED, (ledPin == RED_LED) ? HIGH : LOW);
  digitalWrite(YELLOW_LED, (ledPin == YELLOW_LED) ? HIGH : LOW);
  digitalWrite(GREEN_LED, (ledPin == GREEN_LED) ? HIGH : LOW);
}
